// Digital circuit Registers.dig as structural Verilog
module Registers (
  input  in_1,
  input  clk,
  input  in_7,
  input  clk_2,
  output out_3,
  output out_4,
  output out_5,
  output out_6,
  output out_9,
  output out_10,
  output out_11,
  output out_12
);

  D_FF d_ff_1 (.D(out_9), .C(clk_2), .Q(out_12));  // open: nQ
  D_FF d_ff_2 (.D(in_1), .C(clk), .Q(out_3));  // open: nQ
  D_FF d_ff_3 (.D(out_3), .C(clk), .Q(out_4));  // open: nQ
  D_FF d_ff_4 (.D(out_10), .C(clk_2), .Q(out_9));  // open: nQ
  D_FF d_ff_5 (.D(out_11), .C(clk_2), .Q(out_10));  // open: nQ
  D_FF d_ff_6 (.D(out_4), .C(clk), .Q(out_5));  // open: nQ
  D_FF d_ff_7 (.D(out_5), .C(clk), .Q(out_6));  // open: nQ
  D_FF d_ff_8 (.D(in_7), .C(clk_2), .Q(out_11));  // open: nQ

  // Notes on the sheet:
  //   Right Shifter
  //   Left Shifter
endmodule
