// Digital circuit Registers_n_AddSub.dig as structural Verilog
module Registers_n_AddSub (
  input  in_1,
  input  clk,
  input  in_7,
  input  clk_2,
  input  in_13,
  input  in_14,
  input  in_15,
  input  in_16,
  input  clk_3,
  input  in_18,
  output out_3,
  output out_4,
  output out_5,
  output out_6,
  output out_9,
  output out_10,
  output out_11,
  output out_12,
  output out_19,
  output out_20,
  output out_21,
  output out_22
);

  wire add_1_s, add_2_c_o, add_2_s, add_3_c_o, add_3_s, add_4_c_o, add_4_s, xor_1_out, xor_2_out, xor_3_out,
       xor_4_out;

  D_FF d_ff_1 (.D(out_9), .C(clk_2), .Q(out_12));  // open: nQ
  D_FF d_ff_2 (.D(in_1), .C(clk), .Q(out_3));  // open: nQ
  D_FF d_ff_3 (.D(out_3), .C(clk), .Q(out_4));  // open: nQ
  D_FF d_ff_4 (.D(out_10), .C(clk_2), .Q(out_9));  // open: nQ
  D_FF d_ff_5 (.D(out_11), .C(clk_2), .Q(out_10));  // open: nQ
  D_FF d_ff_6 (.D(out_4), .C(clk), .Q(out_5));  // open: nQ
  D_FF d_ff_7 (.D(out_5), .C(clk), .Q(out_6));  // open: nQ
  D_FF d_ff_8 (.D(in_7), .C(clk_2), .Q(out_11));  // open: nQ
  xor xor_1 (xor_1_out, in_13, in_18);
  xor xor_2 (xor_2_out, in_14, in_18);
  xor xor_3 (xor_3_out, in_15, in_18);
  xor xor_4 (xor_4_out, in_16, in_18);
  Add add_1 (.a(out_19), .b(xor_1_out), .c_i(add_2_c_o), .s(add_1_s));  // open: c_o
  Add add_2 (.a(out_20), .b(xor_2_out), .c_i(add_3_c_o), .s(add_2_s), .c_o(add_2_c_o));
  Add add_3 (.a(out_21), .b(xor_3_out), .c_i(add_4_c_o), .s(add_3_s), .c_o(add_3_c_o));
  Add add_4 (.a(out_22), .b(xor_4_out), .c_i(in_18), .s(add_4_s), .c_o(add_4_c_o));
  D_FF d_ff_9 (.D(add_1_s), .C(clk_3), .Q(out_19));  // open: nQ
  D_FF d_ff_10 (.D(add_2_s), .C(clk_3), .Q(out_20));  // open: nQ
  D_FF d_ff_11 (.D(add_3_s), .C(clk_3), .Q(out_21));  // open: nQ
  D_FF d_ff_12 (.D(add_4_s), .C(clk_3), .Q(out_22));  // open: nQ

  // Notes on the sheet:
  //   Right Shifter
  //   Left Shifter
  //   Add/Sub
endmodule
